// Logisim project CU.circ as structural Verilog: 4 circuits, main circuit CNTR
module CNTR (
  input  in_1,
  output Fetch,
  output Load,
  output Exe,
  output Sav
);

  wire not_1_out, not_2_out, not_3_out, not_4_out, t_ff_1_q, t_ff_1_qn, t_ff_2_q;

  T_Flip_Flop t_ff_1 (.T(1'b1), .clk(in_1), .Q(t_ff_1_q), .Qn(t_ff_1_qn));  // open: reset, preset
  not not_1 (not_1_out, t_ff_2_q);
  not not_2 (not_2_out, t_ff_1_q);
  and and_1 (Fetch, not_2_out, not_1_out);
  T_Flip_Flop t_ff_2 (.T(1'b1), .clk(t_ff_1_qn), .Q(t_ff_2_q));  // open: Qn, reset, preset
  not not_3 (not_3_out, t_ff_2_q);
  not not_4 (not_4_out, t_ff_1_q);
  and and_2 (Load, t_ff_1_q, not_3_out);
  and and_3 (Sav, t_ff_1_q, t_ff_2_q);
  and and_4 (Exe, not_4_out, t_ff_2_q);
endmodule

module OP_ROM (
  input  [7:0] IRin,
  output ADD,
  output SUB,
  output MULT,
  output LD,
  output SAV,
  output BEQ,
  output BNQ,
  output PRT,
  output INP,
  output STOP,
  output FLSH
);

  wire not_1_out, not_2_out, not_3_out, not_4_out, not_5_out, not_6_out, not_7_out, not_8_out, not_9_out,
       not_10_out, not_11_out, not_12_out, not_13_out, not_14_out, not_15_out, not_16_out, not_17_out,
       not_18_out, not_19_out;

  not not_1 (not_1_out, IRin[3]);
  not not_2 (not_2_out, IRin[4]);
  not not_3 (not_3_out, IRin[5]);
  not not_4 (not_4_out, IRin[4]);
  not not_5 (not_5_out, IRin[5]);
  not not_6 (not_6_out, IRin[5]);
  not not_7 (not_7_out, IRin[6]);
  not not_8 (not_8_out, IRin[6]);
  not not_9 (not_9_out, IRin[6]);
  not not_10 (not_10_out, IRin[7]);
  not not_11 (not_11_out, IRin[7]);
  not not_12 (not_12_out, IRin[2]);
  not not_13 (not_13_out, IRin[3]);
  not not_14 (not_14_out, IRin[5]);
  not not_15 (not_15_out, IRin[3]);
  not not_16 (not_16_out, IRin[5]);
  not not_17 (not_17_out, IRin[5]);
  not not_18 (not_18_out, IRin[0]);
  not not_19 (not_19_out, IRin[5]);
  and and_1 (ADD, not_1_out, not_2_out, not_3_out, IRin[6], IRin[7]);
  and and_2 (SUB, IRin[3], not_4_out, not_5_out, IRin[6], IRin[7]);
  and and_3 (MULT, IRin[5], IRin[6], IRin[7]);
  and and_4 (LD, not_6_out, not_7_out, IRin[7]);
  and and_5 (SAV, IRin[5], not_8_out, IRin[7]);
  and and_6 (BEQ, not_9_out, not_10_out);
  and and_7 (BNQ, IRin[6], not_11_out);
  and and_8 (PRT, not_12_out, not_13_out, IRin[4], not_14_out, IRin[6], IRin[7]);
  and and_9 (INP, IRin[2], not_15_out, IRin[4], not_16_out, IRin[6], IRin[7]);
  and and_10 (STOP, IRin[0], IRin[1], IRin[2], IRin[3], IRin[4], not_17_out, IRin[6], IRin[7]);
  and and_11 (FLSH, not_18_out, IRin[1], IRin[2], IRin[3], IRin[4], not_19_out, IRin[6], IRin[7]);
endmodule

module CU (
  input  [7:0] IRin,
  input  in_2,
  output Reg0,
  output Reg1,
  output ALU_L,
  output ALU_R,
  output ALU_O,
  output STAT,
  output IR,
  output PC,
  output MAR,
  output MBR,
  output R_W,
  output ALU_FLAG
);

  wire add_1_done, or_1_out;

  OP_ROM op_rom_1 (.IRin(IRin));  // open: PRT, BEQ, LD, SUB, ADD, MULT, SAV, BNQ, INP, STOP, FLSH
  Clock clock_1 ();  // open: out
  or or_1 (or_1_out, add_1_done, in_2);
  CNTR cntr_1 (.in_1(or_1_out));  // open: Sav, Exe, Load, Fetch
  ADD add_1 (.IRin(IRin), .DONE(add_1_done));  // open: Actv, LOAD, EXE, SAV, R0, R1, R_W, ALU_L, ALU_R, ALU_FLAG, ALU_O

  // Notes on the sheet:
  //   Control Gates
endmodule

module ADD (
  input  [7:0] IRin,
  input  Actv,
  input  LOAD,
  input  EXE,
  input  SAV,
  output DONE,
  output R0,
  output R1,
  output R_W,
  output ALU_L,
  output ALU_R,
  output ALU_FLAG,
  output ALU_O
);

  wire and_1_out, and_2_out, and_3_out, and_4_out, and_5_out, and_6_out, and_7_out, and_8_out, clock_1_out,
       clock_2_out, clock_3_out, not_1_out, not_2_out, not_3_out, or_1_out, or_2_out, or_4_out, or_5_out,
       t_ff_1_qn;

  and and_1 (and_1_out, LOAD, Actv);
  and and_2 (and_2_out, EXE, Actv);
  and and_3 (and_3_out, SAV, Actv);
  or or_1 (or_1_out, ALU_L, ALU_R);
  T_Flip_Flop t_ff_1 (.T(or_2_out), .clk(clock_1_out), .Q(ALU_L), .Qn(t_ff_1_qn), .reset(and_6_out));  // open: preset
  or or_2 (or_2_out, and_6_out, and_1_out);
  Clock clock_1 (.out(clock_1_out));
  T_Flip_Flop t_ff_2 (.T(and_2_out), .clk(clock_2_out), .Q(ALU_FLAG), .reset(and_7_out));  // open: Qn, preset
  Clock clock_2 (.out(clock_2_out));
  not not_1 (not_1_out, clock_2_out);
  T_Flip_Flop t_ff_3 (.T(and_3_out), .clk(clock_3_out), .Q(ALU_O), .reset(and_8_out));  // open: Qn, preset
  Clock clock_3 (.out(clock_3_out));
  not not_2 (not_2_out, clock_3_out);
  T_Flip_Flop t_ff_4 (.T(or_2_out), .clk(t_ff_1_qn), .Q(ALU_R), .reset(and_6_out));  // open: Qn, preset
  and and_4 (and_4_out, IRin[2], ALU_L);
  and and_5 (and_5_out, IRin[1], ALU_R);
  and and_6 (and_6_out, ALU_R, ALU_L);
  or or_3 (DONE, and_6_out, or_4_out);
  or or_4 (or_4_out, and_7_out, and_8_out);
  and and_7 (and_7_out, ALU_FLAG, not_1_out);
  and and_8 (and_8_out, ALU_O, not_2_out);
  Demultiplexer #(.enable("false")) demultiplexer_1 (.out0(R0), .out1(R1), .in(or_1_out), .sel(or_5_out));
  not not_3 (not_3_out, and_1_out);
  or or_5 (or_5_out, and_4_out, and_5_out);
  buf or_6 (R_W, not_3_out);  // OR_Gate
endmodule
